# Fritzing sketch Kapı klidi projesi (saved by Fritzing 0.9.3b)
circuit board: 8.46667cm x 5.64444cm
breadboards: 1

parts:
  Bauteil1 = Arduino Uno (Rev3)
  RC522 = RFID-RC522
  hc-sr1 = hc-sr04
  U1 = TCRT5000 [package=THT]
  Parça1 = Bluetooth HC-05 Macho  # not connected
  SG1 = Buzzer 12mm [package=buzzer-12mm-ns]
  J1 = Basic Servo

nets:
  N1: Bauteil1.A0, U1.Pin_3
  N2: Bauteil1.D9_PWM, RC522.RST
  N3: Bauteil1.D10_PWM/SS, RC522.SDA
  N4: Bauteil1.D11_PWM/MOSI, RC522.MOSI
  N5: Bauteil1.D12/MISO, RC522.MISO
  N6: Bauteil1.D13/SCK, RC522.SCK
  GND: Bauteil1.GND, RC522.GND, hc-sr1.GND, U1.Pin_1, J1.gnd
  N7: Bauteil1.D2, SG1.2
  N8: Bauteil1.D5_PWM, J1.pulse
  N9: Bauteil1.D6_PWM, hc-sr1.Trig
  N10: Bauteil1.D7, hc-sr1.Echo
  VCC: Bauteil1.3V3, Bauteil1.5V, RC522.3_3V, hc-sr1.VCC, U1.Pin_4, J1.vcc

custom parts:
  RFID-RC522: The simple China made RFID reader
  TCRT5000: TCRT5000 optical reflective sensor
